// Logisim project analyzer_7400.circ as structural Verilog: 7 circuits, main circuit main
module mem_16x8 (
  input  [7:0] Din,
  input  [3:0] ADDRin,
  input  [7:0] WORD,
  input  WORDen,
  input  HLT,
  input  CLK,
  input  RUN,
  output [7:0] Dout,
  output [3:0] MEM,
  output RW
);

  wire and4_pin8, and4_pin10, comparator1_pin3, comparator1_pin6, comparator2_pin3, comparator2_pin6,
       counter_pin2, counter_pin9, counter_pin10, mult2to1_pin3, mult2to1_pin6, mult2to1_pin10,
       mult2to1_pin13, mult2to1_pin15, n7414_1_pin8, n7432_1_pin1, n74245_1_pin1, n74245_1_pin19, or1_pin3,
       RAM1_no1, RAM1_no2, RAM1_no3, RAM1_no4, RAM2_no1, RAM2_no2, RAM2_no3, RAM2_no4, SR_p2, SR_p5;

  _7485 comparator1 (
    .pin1(WORD[0]), .pin3(comparator1_pin3), .pin6(comparator1_pin6), .pin15(Din[0]), .pin14(WORD[1]),
    .pin13(Din[1]), .pin12(Din[2]), .pin11(WORD[2]), .pin10(Din[3]), .pin9(WORD[3]));  // open: pin2, pin4, pin5, pin7
  _7485 comparator2 (
    .pin1(WORD[4]), .pin3(comparator2_pin3), .pin6(comparator2_pin6), .pin15(Din[4]), .pin14(WORD[5]),
    .pin13(Din[5]), .pin12(Din[6]), .pin11(WORD[6]), .pin10(Din[7]), .pin9(WORD[7]));  // open: pin2, pin4, pin5, pin7
  _7421 and4 (
    .pin13(comparator1_pin6), .pin12(comparator2_pin6), .pin10(and4_pin10), .pin9(WORDen), .pin8(and4_pin8));  // open: pin1, pin2, pin3, pin4, pin5, pin6, pin11
  _74157 mult2to1 (
    .pin1(RW), .pin2(ADDRin[0]), .pin3(mult2to1_pin3), .pin4(MEM[0]), .pin5(ADDRin[1]), .pin6(mult2to1_pin6),
    .pin7(MEM[1]), .pin15(mult2to1_pin15), .pin14(ADDRin[3]), .pin13(mult2to1_pin13), .pin12(MEM[3]),
    .pin11(ADDRin[2]), .pin10(mult2to1_pin10), .pin9(MEM[2]));
  _74161 counter (
    .pin1(RUN), .pin2(counter_pin2), .pin7(RW), .pin14(mult2to1_pin3), .pin13(mult2to1_pin6),
    .pin12(mult2to1_pin10), .pin11(mult2to1_pin13), .pin10(counter_pin10), .pin9(counter_pin9));  // open: pin3, pin4, pin5, pin6, pin15
  _7432 or1 (
    .pin1(and4_pin8), .pin2(HLT), .pin3(or1_pin3));  // open: pin4, pin5, pin6, pin13, pin12, pin11, pin10, pin9, pin8
  _7414 u_7414_1 (
    .pin1(CLK), .pin2(counter_pin2), .pin9(or1_pin3), .pin8(n7414_1_pin8));  // open: pin3, pin4, pin5, pin6, pin13, pin12, pin11, pin10
  SN74LS189 RAM1 (
    .nCS(1'b0), .nWE(counter_pin2), .A3(MEM[0]), .D4(Din[0]), .A2(MEM[1]), .D3(Din[1]), .A1(MEM[2]),
    .D2(Din[2]), .A0(MEM[3]), .D1(Din[3]), .nO4(RAM1_no4), .nO3(RAM1_no3), .nO2(RAM1_no2), .nO1(RAM1_no1));
  SN74LS189 RAM2 (
    .nCS(1'b0), .nWE(counter_pin2), .A3(MEM[0]), .D4(Din[4]), .A2(MEM[1]), .D3(Din[5]), .A1(MEM[2]),
    .D2(Din[6]), .A0(MEM[3]), .D1(Din[7]), .nO4(RAM2_no4), .nO3(RAM2_no3), .nO2(RAM2_no2), .nO1(RAM2_no1));
  // SN74LS279 SR: pin names not known; wires that end beside it: RUN, SR_p2, SR_p2, n7414_1_pin8, SR_p5, SR_p5, RW
  _74245 u_74245_1 (
    .pin1(n74245_1_pin1), .pin2(RAM1_no4), .pin3(RAM1_no3), .pin4(RAM1_no2), .pin5(RAM1_no1),
    .pin6(RAM2_no4), .pin7(RAM2_no3), .pin8(RAM2_no2), .pin9(RAM2_no1), .pin19(n74245_1_pin19),
    .pin18(Dout[7]), .pin17(Dout[6]), .pin16(Dout[5]), .pin15(Dout[4]), .pin14(Dout[3]), .pin13(Dout[2]),
    .pin12(Dout[1]), .pin11(Dout[0]));
  _7432 u_7432_1 (
    .pin1(n7432_1_pin1), .pin2(RW), .pin3(n74245_1_pin19));  // open: pin4, pin5, pin6, pin13, pin12, pin11, pin10, pin9, pin8
  // also tied to GND on the sheet: {mult2to1_pin15, n7432_1_pin1}
  // also tied to VCC on the sheet: {and4_pin10, comparator1_pin3, comparator2_pin3, counter_pin10, counter_pin9, n74245_1_pin1}

  // Notes on the sheet:
  //   CLK: initial=0x1
  //   RUN: initial=0x1
endmodule

module SN74LS189 (
  input  A3,
  input  A2,
  input  A1,
  input  A0,
  input  nCS,
  input  nWE,
  input  D4,
  input  D3,
  input  D2,
  input  D1,
  output nO4,
  output nO3,
  output nO2,
  output nO1
);

  wire nor_1_out;
  wire [3:0] ram_1_dout;

  nor nor_1 (nor_1_out, nCS, nWE);
  RAM #(.addrWidth(4), .dataWidth(4), .enables("line"), .trigger("high")) ram_1 (
    .addr({A3, A2, A1, A0}), .we(nor_1_out), .clk(1'b1), .din({D4, D3, D2, D1}), .dout(ram_1_dout));
  not not_1 (nO4, ram_1_dout[3]);
  not not_2 (nO3, ram_1_dout[2]);
  not not_3 (nO2, ram_1_dout[1]);
  not not_4 (nO1, ram_1_dout[0]);
endmodule

module SN74LS279 (
  input  S1_1,
  input  S1_2,
  input  R1,
  input  S2,
  input  R2,
  input  S3_1,
  input  S3_2,
  input  R3,
  input  S4,
  input  R4,
  output Q1,
  output Q2,
  output Q3,
  output Q4
);

  wire nor_1_out, nor_2_out, not_1_out, not_2_out, not_3_out, not_4_out, not_5_out, not_6_out;

  S_R_Flip_Flop #(.trigger("low")) s_r_ff_1 (
    .S(nor_1_out), .R(not_1_out), .clk(1'b0), .Q(Q1));  // open: reset, Qn, preset
  nor nor_1 (nor_1_out, S1_1, S1_2);
  not not_1 (not_1_out, R1);
  S_R_Flip_Flop #(.trigger("low")) s_r_ff_2 (
    .S(not_2_out), .R(not_3_out), .clk(1'b0), .Q(Q2));  // open: reset, Qn, preset
  not not_2 (not_2_out, S2);
  not not_3 (not_3_out, R2);
  S_R_Flip_Flop #(.trigger("low")) s_r_ff_3 (
    .S(nor_2_out), .R(not_4_out), .clk(1'b0), .Q(Q3));  // open: reset, Qn, preset
  nor nor_2 (nor_2_out, S3_1, S3_2);
  not not_4 (not_4_out, R3);
  S_R_Flip_Flop #(.trigger("low")) s_r_ff_4 (
    .S(not_5_out), .R(not_6_out), .clk(1'b0), .Q(Q4));  // open: reset, Qn, preset
  not not_5 (not_5_out, S4);
  not not_6 (not_6_out, R4);
endmodule

module main (
  input  [7:0] in_1,
  input  [7:0] in_2,
  output [3:0] out_3
);

  wire button_1_out, button_2_out, button_3_out, button_4_out, button_5_out, button_6_out, button_7_out,
       clock_1_out, mem_16x8_1_rw;
  wire [3:0] disp_16x16_1_addrout;
  wire [7:0] mem_16x8_1_dout;
  wire [15:0] disp_16x16_1_col, disp_16x16_1_row, dotmatrix_1_p2, not_1_out;

  // DipSwitch #(.number(1)) dipswitch_1: pin names not known
  Button button_1 (.out(button_1_out));
  Button button_2 (.out(button_2_out));
  Button button_3 (.out(button_3_out));
  mem_16x8 mem_16x8_1 (
    .Din(in_1), .ADDRin(disp_16x16_1_addrout), .WORD(in_2), .HLT(button_1_out), .CLK(button_2_out),
    .RUN(button_3_out), .Dout(mem_16x8_1_dout), .MEM(out_3), .RW(mem_16x8_1_rw));  // open: WORDen
  Button #(.press("passive")) button_4 (.out(button_4_out));
  Button #(.press("passive")) button_5 (.out(button_5_out));
  Clock clock_1 (.out(clock_1_out));
  Button #(.press("passive")) button_6 (.out(button_6_out));
  Button #(.press("passive")) button_7 (.out(button_7_out));
  disp_16x16 disp_16x16_1 (
    .Xinc(button_4_out), .Xdec(button_5_out), .CLK(clock_1_out), .Din(mem_16x8_1_dout), .Yinc(button_6_out),
    .Ydec(button_7_out), .COL(disp_16x16_1_col), .ADDRout(disp_16x16_1_addrout), .ROW(disp_16x16_1_row));
  assign not_1_out = ~disp_16x16_1_col;  // NOT_Gate not_1, 16 bits wide
  // DotMatrix #(.dotshape("circle"), .inputtype("select"), .matrixcols(16), .matrixrows(16)) dotmatrix_1: pin names not known; wires that end beside it: not_1_out, dotmatrix_1_p2
  assign dotmatrix_1_p2 = mem_16x8_1_rw ? disp_16x16_1_row : 16'bz;  // Controlled_Buffer controlled_buffer_1
endmodule

module mem_64x8 (
  input  [7:0] Din,
  input  [7:0] HLT_word,
  input  HLT_EN,
  input  [5:0] ADDRin,
  input  CLK,
  input  HLT,
  input  RUN,
  output [7:0] Dout
);

  wire n7414_1_pin9, n7421_1_pin8, n7432_1_pin11, n7432_2_pin3, n7432_2_pin6, n7432_2_pin8, n7432_2_pin11,
       n7485_1_pin3, n7485_1_pin6, n7485_2_pin3, n74139_1_pin9, n74139_1_pin10, n74139_1_pin11,
       n74139_1_pin12, n74139_1_pin13, n74139_1_pin14, n74139_1_pin15, n74157_1_pin1, n74157_1_pin3,
       n74157_1_pin6, n74157_1_pin10, n74157_1_pin13, n74157_2_pin3, n74157_2_pin6, n74161_1_pin7,
       n74161_1_pin9, n74161_1_pin10, n74161_1_pin15, n74161_2_pin7, n74161_2_pin9;
  wire [3:0] n74157_1_pin4, undriven;
  wire [7:0] ram_unit_1_dout;

  _7485 u_7485_1 (
    .pin1(HLT_word[4]), .pin3(n7485_1_pin3), .pin6(n7485_1_pin6), .pin15(Din[4]), .pin14(HLT_word[5]),
    .pin13(Din[5]), .pin12(Din[6]), .pin11(HLT_word[6]), .pin10(Din[7]), .pin9(HLT_word[7]));  // open: pin2, pin4, pin5, pin7
  _7485 u_7485_2 (
    .pin1(HLT_word[0]), .pin3(n7485_2_pin3), .pin6(n7485_1_pin6), .pin15(Din[0]), .pin14(HLT_word[1]),
    .pin13(Din[1]), .pin12(Din[2]), .pin11(HLT_word[2]), .pin10(Din[3]), .pin9(HLT_word[3]));  // open: pin2, pin4, pin5, pin7
  _7421 u_7421_1 (
    .pin13(HLT_EN), .pin12(n7485_1_pin6), .pin10(n7485_1_pin6), .pin9(n7485_1_pin6), .pin8(n7421_1_pin8));  // open: pin1, pin2, pin3, pin4, pin5, pin6, pin11
  _74157 u_74157_1 (
    .pin1(n74157_1_pin1), .pin2(ADDRin[0]), .pin3(n74157_1_pin3), .pin4(n74157_1_pin4[0]), .pin5(ADDRin[1]),
    .pin6(n74157_1_pin6), .pin7(n74157_1_pin4[1]), .pin14(ADDRin[3]), .pin13(n74157_1_pin13),
    .pin12(n74157_1_pin4[3]), .pin11(ADDRin[2]), .pin10(n74157_1_pin10), .pin9(n74157_1_pin4[2]));  // open: pin15
  _74161 u_74161_1 (
    .pin1(RUN), .pin2(CLK), .pin7(n74161_1_pin7), .pin15(n74161_1_pin15), .pin14(n74157_1_pin3),
    .pin13(n74157_1_pin6), .pin12(n74157_1_pin10), .pin11(n74157_1_pin13), .pin10(n74161_1_pin10),
    .pin9(n74161_1_pin9));  // open: pin3, pin4, pin5, pin6
  _7432 u_7432_1 (
    .pin13(HLT), .pin12(n7421_1_pin8), .pin11(n7432_1_pin11));  // open: pin1, pin2, pin3, pin4, pin5, pin6, pin10, pin9, pin8
  _74139 u_74139_1 (
    .pin15(n74139_1_pin15), .pin14(n74139_1_pin14), .pin13(n74139_1_pin13), .pin12(n74139_1_pin12),
    .pin11(n74139_1_pin11), .pin10(n74139_1_pin10), .pin9(n74139_1_pin9));  // open: pin1, pin2, pin3, pin4, pin5, pin6, pin7
  _74157 u_74157_2 (
    .pin1(n74157_1_pin1), .pin2(ADDRin[5]), .pin3(n74157_2_pin3), .pin4(n74139_1_pin13), .pin5(ADDRin[4]),
    .pin6(n74157_2_pin6), .pin7(n74139_1_pin14));  // open: pin15, pin14, pin13, pin12, pin11, pin10, pin9
  _74161 u_74161_2 (
    .pin1(RUN), .pin2(CLK), .pin7(n74161_2_pin7), .pin14(n74157_2_pin3), .pin13(n74157_2_pin6),
    .pin10(n74161_1_pin15), .pin9(n74161_2_pin9));  // open: pin3, pin4, pin5, pin6, pin15, pin12, pin11
  SN74LS279 sn74ls279_1 (
    .S4(RUN), .R4(n7414_1_pin9), .Q4(n74157_1_pin1));  // open: S1_2, R1, S2, R2, S3_1, S3_2, R3, S1_1, Q1, Q2, Q3
  _7432 u_7432_2 (
    .pin1(n74157_1_pin1), .pin2(n74139_1_pin10), .pin3(n7432_2_pin3), .pin4(n74157_1_pin1),
    .pin5(n74139_1_pin9), .pin6(n7432_2_pin6), .pin13(n74157_1_pin1), .pin12(n74139_1_pin12),
    .pin11(n7432_2_pin11), .pin10(n74157_1_pin1), .pin9(n74139_1_pin11), .pin8(n7432_2_pin8));
  ram_unit ram_unit_1 (
    .Address(n74157_1_pin4), .Din(Din), .nCS(n74139_1_pin12), .nW(CLK), .nOE(n7432_2_pin11),
    .Dout(ram_unit_1_dout));
  ram_unit ram_unit_2 (
    .Address(n74157_1_pin4), .Din(Din), .nCS(n74139_1_pin11), .nW(CLK), .nOE(n7432_2_pin8),
    .Dout(ram_unit_1_dout));
  ram_unit ram_unit_3 (
    .Address(undriven), .Din(Din), .nCS(n74139_1_pin10), .nW(CLK), .nOE(n7432_2_pin3), .Dout(ram_unit_1_dout));
  ram_unit ram_unit_4 (
    .Address(n74157_1_pin4), .Din(Din), .nCS(n74139_1_pin9), .nW(CLK), .nOE(n7432_2_pin6),
    .Dout(ram_unit_1_dout));
  _7414 u_7414_1 (
    .pin1(ram_unit_1_dout[2]), .pin2(Dout[2]), .pin3(ram_unit_1_dout[3]), .pin4(Dout[3]),
    .pin13(ram_unit_1_dout[1]), .pin12(Dout[1]), .pin11(ram_unit_1_dout[0]), .pin10(Dout[0]),
    .pin9(n7414_1_pin9), .pin8(n74139_1_pin15));  // open: pin5, pin6
  _7414 u_7414_2 (
    .pin1(ram_unit_1_dout[6]), .pin2(Dout[6]), .pin3(ram_unit_1_dout[7]), .pin4(Dout[7]),
    .pin5(n7432_1_pin11), .pin6(n7414_1_pin9), .pin13(ram_unit_1_dout[5]), .pin12(Dout[5]),
    .pin11(ram_unit_1_dout[4]), .pin10(Dout[4]));  // open: pin9, pin8
  // also tied to VCC on the sheet: {n7485_1_pin3, n7485_2_pin3, n74161_1_pin10, n74161_1_pin7, n74161_1_pin9, n74161_2_pin7, n74161_2_pin9}

  // Notes on the sheet:
  //   ADDRin: initial=0x1
  //   RUN: initial=0x1
endmodule

module disp_16x16 (
  input  Xinc,
  input  Xdec,
  input  CLK,
  input  [7:0] Din,
  input  Yinc,
  input  Ydec,
  output [15:0] COL,
  output [3:0] ADDRout,
  output [15:0] ROW
);

  wire n7404_1_pin1, n7404_1_pin12, n74138_1_pin4, n74138_1_pin5, n74138_2_pin4, n74138_2_pin6,
       n74157_1_pin12, n74157_1_pin14, n74157_1_pin15, n74157_2_pin9, n74157_2_pin10, n74157_2_pin15,
       n74161_1_pin1, n74161_1_pin7, n74161_1_pin9, n74161_1_pin10, n74193_1_pin2, n74193_1_pin3,
       n74193_1_pin6, n74193_1_pin7, n74193_1_pin11, n74283_1_pin3, n74283_1_pin5, n74283_1_pin12,
       n74283_1_pin14, SRQ;

  _74193 u_74193_1 (
    .pin2(n74193_1_pin2), .pin3(n74193_1_pin3), .pin4(Xdec), .pin5(Xinc), .pin6(n74193_1_pin6),
    .pin7(n74193_1_pin7), .pin11(n74193_1_pin11));  // open: pin1, pin15, pin14, pin13, pin12, pin10, pin9
  _74283 u_74283_1 (
    .pin1(ADDRout[1]), .pin2(n74193_1_pin2), .pin3(n74283_1_pin3), .pin4(ADDRout[0]), .pin5(n74283_1_pin5),
    .pin6(n74193_1_pin3), .pin15(n74193_1_pin6), .pin14(n74283_1_pin14), .pin13(ADDRout[2]),
    .pin12(n74283_1_pin12), .pin11(n74193_1_pin7), .pin10(ADDRout[3]));  // open: pin7, pin9
  _74161 u_74161_1 (
    .pin1(n74161_1_pin1), .pin2(CLK), .pin7(n74161_1_pin7), .pin14(n74283_1_pin5), .pin13(n74283_1_pin3),
    .pin12(n74283_1_pin14), .pin11(n74283_1_pin12), .pin10(n74161_1_pin10), .pin9(n74161_1_pin9));  // open: pin3, pin4, pin5, pin6, pin15
  _74157 u_74157_1 (
    .pin1(SRQ), .pin2(Din[5]), .pin3(Din[1]), .pin4(ROW[7]), .pin5(Din[6]), .pin6(Din[2]), .pin7(ROW[9]),
    .pin15(n74157_1_pin15), .pin14(n74157_1_pin14), .pin13(Din[4]), .pin12(n74157_1_pin12), .pin11(Din[7]),
    .pin10(Din[3]), .pin9(ROW[12]));
  SN74LS279 sn74ls279_1 (
    .S1_2(Ydec), .R1(Yinc), .S1_1(Ydec), .Q1(SRQ));  // open: S2, R2, S3_1, S3_2, R3, S4, R4, Q2, Q3, Q4
  _74138 u_74138_1 (
    .pin1(n74283_1_pin5), .pin2(n74283_1_pin3), .pin3(n74283_1_pin14), .pin4(n74138_1_pin4),
    .pin5(n74138_1_pin5), .pin6(n74283_1_pin12), .pin7(COL[15]), .pin15(COL[8]), .pin14(COL[9]),
    .pin13(COL[10]), .pin12(COL[11]), .pin11(COL[12]), .pin10(COL[13]), .pin9(COL[14]));
  _74138 u_74138_2 (
    .pin1(n74283_1_pin5), .pin2(n74283_1_pin3), .pin3(n74283_1_pin14), .pin4(n74138_2_pin4),
    .pin5(n74283_1_pin12), .pin6(n74138_2_pin6), .pin7(COL[7]), .pin15(COL[0]), .pin14(COL[1]),
    .pin13(COL[2]), .pin12(COL[3]), .pin11(COL[4]), .pin10(COL[5]), .pin9(COL[6]));
  _74157 u_74157_2 (
    .pin1(SRQ), .pin2(Din[4]), .pin3(Din[0]), .pin4(ROW[4]), .pin15(n74157_2_pin15), .pin11(Din[3]),
    .pin10(n74157_2_pin10), .pin9(n74157_2_pin9));  // open: pin5, pin6, pin7, pin14, pin13, pin12
  _7404 u_7404_1 (
    .pin1(n7404_1_pin1), .pin2(ROW[1]), .pin13(SRQ), .pin12(n7404_1_pin12));  // open: pin3, pin4, pin5, pin6, pin11, pin10, pin9, pin8
  _7432 u_7432_1 (
    .pin13(n74157_1_pin12), .pin12(n7404_1_pin12), .pin11(ROW[15]));  // open: pin1, pin2, pin3, pin4, pin5, pin6, pin10, pin9, pin8
  _7486 u_7486_1 (
    .pin13(n7404_1_pin12), .pin12(n74157_2_pin9), .pin11(n7404_1_pin1));  // open: pin1, pin2, pin3, pin4, pin5, pin6, pin10, pin9, pin8
  _7404 u_7404_2 (
    .pin1(n74157_2_pin9), .pin2(ROW[0]), .pin3(ROW[4]), .pin4(ROW[3]), .pin5(ROW[7]), .pin6(ROW[6]),
    .pin13(n74157_1_pin12), .pin12(ROW[14]), .pin11(ROW[12]), .pin10(ROW[11]), .pin9(ROW[9]), .pin8(ROW[8]));

  assign {ROW[13], ROW[10], ROW[5], ROW[2]} = 4'b0000;
  // also tied to GND on the sheet: {n74157_1_pin15, n74157_1_pin14, n74138_1_pin4, n74138_2_pin4, n74157_2_pin15, n74138_1_pin5, n74157_2_pin10}
  // also tied to VCC on the sheet: {n74161_1_pin1, n74193_1_pin11, n74161_1_pin10, n74161_1_pin7, n74161_1_pin9, n74138_2_pin6}

  // Other names for the same wires on the sheet: D0 = Din[0]; D3 = Din[3]; D4 = Din[4]; O0 = ROW[1]

  // Notes on the sheet:
  //   Yinc: initial=0x1
  //   Ydec: initial=0x1
endmodule

module ram_unit (
  input  [3:0] Address,
  input  [7:0] Din,
  input  nCS,
  input  nW,
  input  nOE,
  output [7:0] Dout
);

  wire n74245_1_pin1, sn74ls189_1_no1, sn74ls189_1_no2, sn74ls189_1_no3, sn74ls189_1_no4, sn74ls189_2_no1,
       sn74ls189_2_no2, sn74ls189_2_no3, sn74ls189_2_no4;

  SN74LS189 sn74ls189_1 (
    .nCS(nCS), .nWE(nW), .A3(Address[3]), .D4(Din[7]), .A2(Address[2]), .D3(Din[6]), .A1(Address[1]),
    .D2(Din[5]), .A0(Address[0]), .D1(Din[4]), .nO4(sn74ls189_1_no4), .nO3(sn74ls189_1_no3),
    .nO2(sn74ls189_1_no2), .nO1(sn74ls189_1_no1));
  SN74LS189 sn74ls189_2 (
    .nCS(nCS), .nWE(nW), .A3(Address[3]), .D4(Din[3]), .A2(Address[2]), .D3(Din[2]), .A1(Address[1]),
    .D2(Din[1]), .A0(Address[0]), .D1(Din[0]), .nO4(sn74ls189_2_no4), .nO3(sn74ls189_2_no3),
    .nO2(sn74ls189_2_no2), .nO1(sn74ls189_2_no1));
  _74245 u_74245_1 (
    .pin1(n74245_1_pin1), .pin2(Dout[0]), .pin3(Dout[1]), .pin4(Dout[2]), .pin5(Dout[3]), .pin6(Dout[4]),
    .pin7(Dout[5]), .pin8(Dout[6]), .pin9(Dout[7]), .pin19(nOE), .pin18(sn74ls189_1_no4),
    .pin17(sn74ls189_1_no3), .pin16(sn74ls189_1_no2), .pin15(sn74ls189_1_no1), .pin14(sn74ls189_2_no4),
    .pin13(sn74ls189_2_no3), .pin12(sn74ls189_2_no2), .pin11(sn74ls189_2_no1));
  // also tied to GND on the sheet: n74245_1_pin1
endmodule
