// Logisim project analyzer_ttl.circ as structural Verilog: 8 circuits, main circuit main
module main (
  input  [7:0] in_1
);

  wire button_1_out, button_2_out, button_3_out, button_4_out, button_5_out, button_6_out, button_7_out,
       clock_1_out, dipswitch_2_sw1, mem_64x8_async_1_fin;
  wire [5:0] disp_16x32_1_addrout;
  wire [7:0] dipswitch_1_sw8, mem_64x8_async_1_dout;
  wire [15:0] controlled_buffer_1_out, disp_16x32_1_dout;
  wire [31:0] disp_16x32_1_colout;

  Button button_1 (.out(button_1_out));
  // DotMatrix #(.dotshape("circle"), .inputtype("select"), .matrixcols(32), .matrixrows(16)) dotmatrix_1: pin names not known
  Button button_2 (.out(button_2_out));
  Button button_3 (.out(button_3_out));
  DipSwitch dipswitch_1 (
    .sw1(dipswitch_1_sw8[7]), .sw2(dipswitch_1_sw8[6]), .sw3(dipswitch_1_sw8[5]), .sw4(dipswitch_1_sw8[4]),
    .sw5(dipswitch_1_sw8[3]), .sw6(dipswitch_1_sw8[2]), .sw7(dipswitch_1_sw8[1]), .sw8(dipswitch_1_sw8[0]));
  mem_64x8_async mem_64x8_async_1 (
    .Din(dipswitch_1_sw8), .EN_HLT(dipswitch_2_sw1), .CLK(button_1_out), .HLT(button_3_out),
    .RUN(button_2_out), .ADDRin(disp_16x32_1_addrout), .WORD(in_1), .FIN(mem_64x8_async_1_fin),
    .Dout(mem_64x8_async_1_dout));  // open: MEM
  DipSwitch #(.number(1)) dipswitch_2 (.sw1(dipswitch_2_sw1));
  Clock clock_1 (.out(clock_1_out));
  disp_16x32 disp_16x32_1 (
    .Yinc(button_4_out), .Ydec(button_6_out), .not_rst(mem_64x8_async_1_fin), .Din(mem_64x8_async_1_dout),
    .CLK(clock_1_out), .Xinc(button_7_out), .Xdec(button_5_out), .ADDRout(disp_16x32_1_addrout),
    .Dout(disp_16x32_1_dout), .COLout(disp_16x32_1_colout));
  Button button_4 (.out(button_4_out));
  Button button_5 (.out(button_5_out));
  Button button_6 (.out(button_6_out));
  assign controlled_buffer_1_out = mem_64x8_async_1_fin ? disp_16x32_1_dout : 16'bz;  // Controlled_Buffer controlled_buffer_1
  Button button_7 (.out(button_7_out));
endmodule

module disp_16x16 (
  input  Xinc,
  input  Xdec,
  input  CLK,
  input  [7:0] Din,
  input  Yinc,
  input  Ydec,
  output [3:0] ADDRout,
  output [15:0] COLout,
  output [15:0] Dout
);

  wire or_1_out, s_r_ff_1_qn;
  wire [3:0] counter_1_q;
  wire [5:0] incrementer_1_offset;

  incrementer incrementer_1 (.dec(Xdec), .inc(Xinc), .offset(incrementer_1_offset));  // open: rst
  Counter #(.max('hf), .width(4)) counter_1 (.Q(counter_1_q), .clk(CLK));  // open: load, D, count, carry, up, clr
  Adder #(.width(4)) adder_1 (.a(incrementer_1_offset[5:2]), .b(counter_1_q), .out(ADDRout));  // open: cin, cout
  S_R_Flip_Flop s_r_ff_1 (.S(Yinc), .R(Ydec), .clk(or_1_out), .Qn(s_r_ff_1_qn));  // open: Q, reset, preset
  or or_1 (or_1_out, Ydec, Yinc);
  Multiplexer #(.width(6)) multiplexer_1 (
    .in0({Din[2], Din[3], Din[4], Din[5], Din[6], Din[7]}),
    .in1({Din[0], Din[1], Din[2], Din[3], Din[4], Din[5]}),
    .out({Dout[1], Dout[4], Dout[7], Dout[9], Dout[12], Dout[15]}), .sel(s_r_ff_1_qn));
  Decoder #(.enable("false"), .select(4)) decoder_1 (
    .out0(COLout[0]), .out1(COLout[1]), .out2(COLout[2]), .out3(COLout[3]), .out4(COLout[4]),
    .out5(COLout[5]), .out6(COLout[6]), .out7(COLout[7]), .out8(COLout[8]), .out9(COLout[9]),
    .out10(COLout[10]), .out11(COLout[11]), .out12(COLout[12]), .out13(COLout[13]), .out14(COLout[14]),
    .out15(COLout[15]), .sel(counter_1_q));
  not not_1 (Dout[14], Dout[15]);
  not not_2 (Dout[11], Dout[12]);
  not not_3 (Dout[8], Dout[9]);
  not not_4 (Dout[6], Dout[7]);
  not not_5 (Dout[3], Dout[4]);
  not not_6 (Dout[0], Dout[1]);
  // DotMatrix #(.dotshape("circle"), .inputtype("select"), .matrixcols(16), .matrixrows(16)) dotmatrix_1: pin names not known; wires that end beside it: COLout, {Dout[15:14], 1'b0, Dout[12:11], 1'b0, Dout[9:6], 1'b0, Dout[4:3], 1'b0, Dout[1:0]}

  assign {Dout[13], Dout[10], Dout[5], Dout[2]} = 4'b0000;
endmodule

module incrementer (
  input  dec,
  input  inc,
  input  rst,
  output [5:0] offset
);

  wire or_1_out;

  Counter #(.max('h3f), .width(6)) counter_1 (
    .Q(offset), .up(inc), .clk(or_1_out), .clr(rst));  // open: load, D, count, carry
  or or_1 (or_1_out, dec, inc);
endmodule

module mem_16x8 (
  input  [7:0] Din,
  input  [7:0] WORD,
  input  HLT,
  input  RUN,
  input  [3:0] ADDRin,
  input  CLK,
  output [3:0] MEM,
  output FIN,
  output [7:0] Dout
);

  wire and_1_out, comparator_1_eq, counter_1_carry, d_ff_1_q, not_1_out, or_1_out, s_r_ff_1_qn;
  wire [3:0] counter_1_q;

  Comparator #(.mode("unsigned")) comparator_1 (.a(Din), .b(WORD), .eq(comparator_1_eq));  // open: gt, lt
  or or_1 (or_1_out, HLT, comparator_1_eq);
  D_Flip_Flop #(.trigger("falling")) d_ff_1 (.clk(CLK), .D(or_1_out), .Q(d_ff_1_q));  // open: Qn, preset, reset
  S_R_Flip_Flop #(.trigger("high")) s_r_ff_1 (
    .S(d_ff_1_q), .R(RUN), .clk(1'b1), .Q(FIN), .Qn(s_r_ff_1_qn));  // open: reset, preset
  and and_1 (and_1_out, s_r_ff_1_qn, CLK);
  Counter #(.max('hf), .width(4)) counter_1 (
    .load(1'b0), .count(1'b1), .Q(counter_1_q), .carry(counter_1_carry), .up(1'b1), .clk(and_1_out), .clr(RUN));  // open: D
  not not_1 (not_1_out, and_1_out);
  RAM #(.addrWidth(4), .dataWidth(4), .enables("line")) ram_1 (
    .addr(MEM), .we(s_r_ff_1_qn), .clk(not_1_out), .din(Din[7:4]), .dout(Dout[3:0]));
  RAM #(.addrWidth(4), .dataWidth(4), .enables("line")) ram_2 (
    .addr(MEM), .we(s_r_ff_1_qn), .clk(not_1_out), .din(Din[3:0]), .dout(Dout[7:4]));
  Multiplexer #(.width(4)) multiplexer_1 (.in0(ADDRin), .in1(counter_1_q), .out(MEM), .sel(s_r_ff_1_qn));
endmodule

module mem_32x8 (
  input  [7:0] WORD,
  input  [7:0] Din,
  input  HLT,
  input  CLK,
  input  RUN,
  input  [4:0] ADDRin,
  output [4:0] MEM,
  output FIN,
  output [7:0] Dout
);

  wire and_1_out, and_2_out, and_3_out, comparator_1_eq, d_ff_1_q, not_1_out, not_2_out, not_3_out, or_1_out,
       s_r_ff_1_qn;
  wire [3:0] A1_dout, A2_dout, B1_dout, B2_dout;
  wire [4:0] counter_1_q;

  Comparator #(.mode("unsigned")) comparator_1 (.a(Din), .b(WORD), .eq(comparator_1_eq));  // open: gt, lt
  or or_1 (or_1_out, HLT, comparator_1_eq);
  D_Flip_Flop #(.trigger("falling")) d_ff_1 (.clk(CLK), .D(or_1_out), .Q(d_ff_1_q));  // open: Qn, preset, reset
  S_R_Flip_Flop #(.trigger("high")) s_r_ff_1 (
    .S(d_ff_1_q), .R(RUN), .clk(1'b1), .Q(FIN), .Qn(s_r_ff_1_qn));  // open: reset, preset
  and and_1 (and_1_out, CLK, s_r_ff_1_qn);
  not not_1 (not_1_out, and_1_out);
  Multiplexer #(.width(5)) multiplexer_1 (.in0(counter_1_q), .in1(ADDRin), .out(MEM), .sel(not_2_out));
  not not_2 (not_2_out, s_r_ff_1_qn);
  Counter #(.max('h1f), .width(5)) counter_1 (
    .Q(counter_1_q), .clk(and_1_out), .clr(RUN));  // open: load, D, count, carry, up
  and and_2 (and_2_out, s_r_ff_1_qn, MEM[4]);
  and and_3 (and_3_out, s_r_ff_1_qn, not_3_out);
  RAM #(.addrWidth(4), .dataWidth(4), .enables("line")) A1 (
    .addr(MEM[3:0]), .we(and_2_out), .clk(not_1_out), .din(Din[7:4]), .dout(A1_dout));
  RAM #(.addrWidth(4), .dataWidth(4), .enables("line")) A2 (
    .addr(MEM[3:0]), .we(and_3_out), .clk(not_1_out), .din(Din[3:0]), .dout(A2_dout));
  RAM #(.addrWidth(4), .dataWidth(4), .enables("line")) B1 (
    .addr(MEM[3:0]), .we(and_2_out), .clk(not_1_out), .din(Din[7:4]), .dout(B1_dout));
  RAM #(.addrWidth(4), .dataWidth(4), .enables("line")) B2 (
    .addr(MEM[3:0]), .we(and_3_out), .clk(not_1_out), .din(Din[3:0]), .dout(B2_dout));
  not not_3 (not_3_out, MEM[4]);
  Multiplexer #(.width(8)) multiplexer_2 (.in0({B1_dout, A1_dout}), .in1({B2_dout, A2_dout}), .out(Dout), .sel(MEM[4]));
endmodule

module mem_64x8 (
  input  [7:0] WORD,
  input  [7:0] Din,
  input  HLT,
  input  CLK,
  input  RUN,
  input  [5:0] ADDRin,
  output FIN,
  output [5:0] MEM,
  output [7:0] Dout
);

  wire and_1_out, comparator_1_eq, d_ff_1_q, decoder_1_out0, decoder_1_out1, decoder_1_out2, decoder_1_out3,
       not_1_out, not_2_out, or_1_out, s_r_ff_1_qn;
  wire [3:0] A1_dout, A2_dout, A3_dout, A4_dout, B1_dout, B2_dout, B3_dout, B4_dout;
  wire [5:0] counter_1_q, register_1_q, subtractor_1_out, subtractor_2_out;

  Comparator #(.mode("unsigned")) comparator_1 (.a(Din), .b(WORD), .eq(comparator_1_eq));  // open: gt, lt
  or or_1 (or_1_out, HLT, comparator_1_eq);
  D_Flip_Flop #(.trigger("falling")) d_ff_1 (.clk(CLK), .D(or_1_out), .Q(d_ff_1_q));  // open: Qn, preset, reset
  S_R_Flip_Flop #(.trigger("high")) s_r_ff_1 (
    .S(d_ff_1_q), .R(RUN), .clk(1'b1), .Q(FIN), .Qn(s_r_ff_1_qn));  // open: reset, preset
  and and_1 (and_1_out, CLK, s_r_ff_1_qn);
  RAM #(.addrWidth(4), .dataWidth(4), .enables("line")) A1 (
    .addr(MEM[3:0]), .we(decoder_1_out0), .clk(not_1_out), .din(Din[7:4]), .dout(A1_dout));
  RAM #(.addrWidth(4), .dataWidth(4), .enables("line")) A2 (
    .addr(MEM[3:0]), .we(decoder_1_out1), .clk(not_1_out), .din(Din[7:4]), .dout(A2_dout));
  RAM #(.addrWidth(4), .dataWidth(4), .enables("line")) A3 (
    .addr(MEM[3:0]), .we(decoder_1_out2), .clk(not_1_out), .din(Din[7:4]), .dout(A3_dout));
  RAM #(.addrWidth(4), .dataWidth(4), .enables("line")) A4 (
    .addr(MEM[3:0]), .we(decoder_1_out3), .clk(not_1_out), .din(Din[7:4]), .dout(A4_dout));
  RAM #(.addrWidth(4), .dataWidth(4), .enables("line")) B1 (
    .addr(MEM[3:0]), .we(decoder_1_out0), .clk(not_1_out), .din(Din[3:0]), .dout(B1_dout));
  RAM #(.addrWidth(4), .dataWidth(4), .enables("line")) B2 (
    .addr(MEM[3:0]), .we(decoder_1_out1), .clk(not_1_out), .din(Din[3:0]), .dout(B2_dout));
  RAM #(.addrWidth(4), .dataWidth(4), .enables("line")) B3 (
    .addr(MEM[3:0]), .we(decoder_1_out2), .clk(not_1_out), .din(Din[3:0]), .dout(B3_dout));
  RAM #(.addrWidth(4), .dataWidth(4), .enables("line")) B4 (
    .addr(MEM[3:0]), .we(decoder_1_out3), .clk(not_1_out), .din(Din[3:0]), .dout(B4_dout));
  Decoder #(.select(2)) decoder_1 (
    .out0(decoder_1_out0), .out1(decoder_1_out1), .out2(decoder_1_out2), .out3(decoder_1_out3),
    .sel(MEM[5:4]), .en(s_r_ff_1_qn));
  not not_1 (not_1_out, and_1_out);
  Multiplexer #(.width(6)) multiplexer_1 (.in0(counter_1_q), .in1(subtractor_1_out), .out(MEM), .sel(not_2_out));
  Counter #(.max('h3f), .width(6)) counter_1 (
    .Q(counter_1_q), .clk(and_1_out), .clr(RUN));  // open: load, D, count, carry, up
  not not_2 (not_2_out, s_r_ff_1_qn);
  Subtractor #(.width(6)) subtractor_1 (.a(ADDRin), .b(register_1_q), .out(subtractor_1_out));  // open: bin, bout
  Subtractor #(.width(6)) subtractor_2 (.a(6'b011110), .b(MEM), .out(subtractor_2_out));  // open: bin, bout
  Subtractor #(.width(6)) subtractor_3 (.bout(or_1_out));  // open: a, b, out, bin
  Register #(.width(6)) register_1 (.D(subtractor_2_out), .en(or_1_out), .clk(CLK), .Q(register_1_q));  // open: clr
  Multiplexer #(.select(2), .width(8)) multiplexer_2 (
    .in0({A1_dout, B1_dout}), .in1({A2_dout, B2_dout}), .in2({B3_dout, A3_dout}), .in3({B4_dout, A4_dout}),
    .out(Dout), .sel(MEM[5:4]));
endmodule

module disp_16x32 (
  input  not_rst,
  input  Xinc,
  input  Xdec,
  input  CLK,
  input  [7:0] Din,
  input  Yinc,
  input  Ydec,
  output [5:0] ADDRout,
  output [31:0] COLout,
  output [15:0] Dout
);

  wire not_1_out, or_1_out, s_r_ff_1_q, s_r_ff_1_qn;
  wire [4:0] counter_1_q;
  wire [5:0] incrementer_1_offset, multiplexer_1_out;

  not not_1 (not_1_out, not_rst);
  Counter #(.max('h1f), .width(5)) counter_1 (.Q(counter_1_q), .clk(CLK));  // open: load, D, count, carry, up, clr
  incrementer incrementer_1 (.dec(Xdec), .inc(Xinc), .rst(not_1_out), .offset(incrementer_1_offset));
  S_R_Flip_Flop s_r_ff_1 (.S(Yinc), .R(Ydec), .clk(or_1_out), .Q(s_r_ff_1_q), .Qn(s_r_ff_1_qn));  // open: reset, preset
  or or_1 (or_1_out, Ydec, Yinc);
  Adder #(.width(6)) adder_1 (.a(incrementer_1_offset), .b({1'b0, counter_1_q}), .out(ADDRout));  // open: cin, cout
  Multiplexer #(.width(6)) multiplexer_1 (
    .in0({Din[3], Din[4], Din[5], Din[6], Din[7], 1'b0}),
    .in1({1'b0, Din[0], Din[1], Din[2], Din[3], Din[4]}),
    .out({multiplexer_1_out[5], Dout[4], Dout[7], Dout[9], Dout[12], multiplexer_1_out[0]}), .sel(s_r_ff_1_qn));
  or or_2 (Dout[15], s_r_ff_1_q, multiplexer_1_out[0]);
  Decoder #(.enable("false"), .select(5)) decoder_1 (
    .out0(COLout[0]), .out1(COLout[1]), .out2(COLout[2]), .out3(COLout[3]), .out4(COLout[4]),
    .out5(COLout[5]), .out6(COLout[6]), .out7(COLout[7]), .out8(COLout[8]), .out9(COLout[9]),
    .out10(COLout[10]), .out11(COLout[11]), .out12(COLout[12]), .out13(COLout[13]), .out14(COLout[14]),
    .out15(COLout[15]), .out16(COLout[16]), .out17(COLout[17]), .out18(COLout[18]), .out19(COLout[19]),
    .out20(COLout[20]), .out21(COLout[21]), .out22(COLout[22]), .out23(COLout[23]), .out24(COLout[24]),
    .out25(COLout[25]), .out26(COLout[26]), .out27(COLout[27]), .out28(COLout[28]), .out29(COLout[29]),
    .out30(COLout[30]), .out31(COLout[31]), .sel(counter_1_q));
  not not_2 (Dout[14], multiplexer_1_out[0]);
  not not_3 (Dout[11], Dout[12]);
  not not_4 (Dout[8], Dout[9]);
  not not_5 (Dout[6], Dout[7]);
  not not_6 (Dout[3], Dout[4]);
  not not_7 (Dout[0], multiplexer_1_out[5]);
  nor nor_1 (Dout[1], Dout[4], s_r_ff_1_q);

  assign {Dout[13], Dout[10], Dout[5], Dout[2]} = 4'b0000;
endmodule

module mem_64x8_async (
  input  HLT,
  input  [7:0] WORD,
  input  [7:0] Din,
  input  EN_HLT,
  input  CLK,
  input  RUN,
  input  [5:0] ADDRin,
  output FIN,
  output [5:0] MEM,
  output [7:0] Dout
);

  wire and_1_out, and_2_out, button_1_out, button_2_out, comparator_1_eq, d_ff_1_q, decoder_1_out0,
       decoder_1_out1, decoder_1_out2, decoder_1_out3, not_1_out, not_2_out, or_1_out, or_2_out, or_3_out,
       or_4_out, s_r_ff_1_qn;
  wire [3:0] A1_dout, A2_dout, A3_dout, A4_dout, B1_dout, B2_dout, B3_dout, B4_dout;
  wire [5:0] counter_1_q, END_OFFSET_q, subtractor_1_out, subtractor_2_out;

  Button button_1 (.out(button_1_out));
  or or_1 (or_1_out, button_1_out, HLT);
  Comparator #(.mode("unsigned")) comparator_1 (.a(Din), .b(WORD), .eq(comparator_1_eq));  // open: gt, lt
  and and_1 (and_1_out, comparator_1_eq, EN_HLT);
  or or_2 (or_2_out, or_1_out, and_1_out);
  or or_3 (or_3_out, or_2_out, or_4_out, or_4_out);
  D_Flip_Flop d_ff_1 (.clk(or_3_out), .D(or_2_out), .Q(d_ff_1_q));  // open: Qn, preset, reset
  or or_4 (or_4_out, button_2_out, RUN);
  Button button_2 (.out(button_2_out));
  S_R_Flip_Flop #(.trigger("high")) s_r_ff_1 (
    .S(d_ff_1_q), .R(or_4_out), .clk(1'b1), .Q(FIN), .Qn(s_r_ff_1_qn));  // open: reset, preset
  and and_2 (and_2_out, CLK, s_r_ff_1_qn);
  Counter #(.max('h3f), .width(6)) counter_1 (
    .Q(counter_1_q), .clk(and_2_out), .clr(or_4_out));  // open: load, D, count, carry, up
  RAM #(.addrWidth(4), .dataWidth(4), .enables("line")) A1 (
    .addr(MEM[3:0]), .we(decoder_1_out0), .clk(not_1_out), .din(Din[7:4]), .dout(A1_dout));
  RAM #(.addrWidth(4), .dataWidth(4), .enables("line")) A2 (
    .addr(MEM[3:0]), .we(decoder_1_out1), .clk(not_1_out), .din(Din[7:4]), .dout(A2_dout));
  RAM #(.addrWidth(4), .dataWidth(4), .enables("line")) A3 (
    .addr(MEM[3:0]), .we(decoder_1_out2), .clk(not_1_out), .din(Din[7:4]), .dout(A3_dout));
  RAM #(.addrWidth(4), .dataWidth(4), .enables("line")) A4 (
    .addr(MEM[3:0]), .we(decoder_1_out3), .clk(not_1_out), .din(Din[7:4]), .dout(A4_dout));
  RAM #(.addrWidth(4), .dataWidth(4), .enables("line")) B1 (
    .addr(MEM[3:0]), .we(decoder_1_out0), .clk(not_1_out), .din(Din[3:0]), .dout(B1_dout));
  RAM #(.addrWidth(4), .dataWidth(4), .enables("line")) B2 (
    .addr(MEM[3:0]), .we(decoder_1_out1), .clk(not_1_out), .din(Din[3:0]), .dout(B2_dout));
  RAM #(.addrWidth(4), .dataWidth(4), .enables("line")) B3 (
    .addr(MEM[3:0]), .we(decoder_1_out2), .clk(not_1_out), .din(Din[3:0]), .dout(B3_dout));
  RAM #(.addrWidth(4), .dataWidth(4), .enables("line")) B4 (
    .addr(MEM[3:0]), .we(decoder_1_out3), .clk(not_1_out), .din(Din[3:0]), .dout(B4_dout));
  Decoder #(.select(2)) decoder_1 (
    .out0(decoder_1_out0), .out1(decoder_1_out1), .out2(decoder_1_out2), .out3(decoder_1_out3),
    .sel(MEM[5:4]), .en(s_r_ff_1_qn));
  not not_1 (not_1_out, and_2_out);
  Multiplexer #(.width(6)) multiplexer_1 (.in0(counter_1_q), .in1(subtractor_1_out), .out(MEM), .sel(not_2_out));
  not not_2 (not_2_out, s_r_ff_1_qn);
  Subtractor #(.width(6)) subtractor_1 (.a(ADDRin), .b(END_OFFSET_q), .out(subtractor_1_out));  // open: bin, bout
  Register #(.width(6)) END_OFFSET (
    .D(subtractor_2_out), .en(or_2_out), .clk(or_2_out), .Q(END_OFFSET_q));  // open: clr
  Subtractor #(.width(6)) subtractor_2 (.a(6'b011110), .b(MEM), .out(subtractor_2_out));  // open: bin, bout
  Multiplexer #(.select(2), .width(8)) multiplexer_2 (
    .in0({A1_dout, B1_dout}), .in1({A2_dout, B2_dout}), .in2({B3_dout, A3_dout}), .in3({B4_dout, A4_dout}),
    .out(Dout), .sel(MEM[5:4]));
endmodule
